// Digital circuit addr_gen.dig as structural Verilog
module addr_gen (
  input  [3:0] data__bus,
  input  clk,
  input  reset,
  input  use__pc,
  input  load__mar,
  output [3:0] addr__bus
);

  wire not_1_out;
  wire [3:0] mar, pc;

  // program_ctr program_ctr_1: pin names not known; wires that end beside it: use__pc, reset, clk, pc
  // four_bit_reg four_bit_reg_1: pin names not known; wires that end beside it: data__bus, load__mar, reset, clk, mar
  not not_1 (not_1_out, use__pc);
  four_bit_mux four_bit_mux_1 (.a(pc), .b(mar), .sel(not_1_out), .y(addr__bus));
endmodule
